# Fritzing sketch driver-pcb (saved by Fritzing 0.9.3b)
circuit board: 7cm x 5cm
breadboards: 1

parts:
  Q1 = Basic FET N-Channel [package="TO220 [THT]"]
  D1 = Rectifier Diode [part_number=1N4004 package="300 mil [THT]"]
  R1 = Resistor [tolerance=±5% resistance=470 package=THT]
  R2 = Resistor [tolerance=±5% resistance=10k package=THT]
  J1 = female pin header, 4 pins [form="♀ (female)"]
  J2 = female pin header, 6 pins [form="♀ (female)"]
  J3 = female pin header, 2 pins [form="♀ (female)"]
  Q2 = Basic FET P-Channel [package="TO220 [THT]"]
  D2 = Rectifier Diode [part_number=1N4001 package="300 mil [THT]"]
  R3 = Resistor [tolerance=±5% resistance=220 package=THT]
  R4 = Resistor [tolerance=±5% resistance=220 package=THT]
  Q3 = Basic FET P-Channel [package="TO220 [THT]"]
  R5 = Resistor [tolerance=±5% resistance=220 package=THT]
  R6 = Resistor [tolerance=±5% resistance=220 package=THT]
  D3 = Rectifier Diode [part_number=1N4001 package="300 mil [THT]"]

nets:
  N1: Q1.gate, R1.Pin_0, R2.Pin_0
  N2: Q1.drain, D1.anode, J2.pin1
  N3: Q1.source, R2.Pin_1, J1.pin4, J3.pin2, Q2.source, R4.Pin_1
  N4: D1.cathode, J2.pin2, J2.pin4, J2.pin6, J3.pin1, D2.cathode, D3.cathode
  N5: R1.Pin_1, J1.pin1
  N6: J1.pin2, R3.Pin_1
  N7: J1.pin3, R5.Pin_1
  N8: J2.pin3, Q2.drain, D2.anode
  N9: J2.pin5, Q3.drain, D3.anode
  N10: Q2.gate, R3.Pin_0, R4.Pin_0
  N11: Q3.gate, R5.Pin_0, R6.Pin_0
  N12: Q3.source, R6.Pin_1

notes:
  12V
  Solenoid 1
  Solenoid 2
  Solenoid 3
